# Fritzing sketch NodeSensor (saved by Fritzing 0.9.3b)
breadboards: 1

parts:
  part = DOIT Esp32 DevKit v1 (30 pins long, 11 pins width)
  part_2 = MicroSD Card Module
  part_3 = DHT22 module

nets:
  3V3: part.3V3, part_2.VCC, part_3.+
  GND: part.GND, part_2.GND, part_3.-
  N1: part.D4, part_3.Out
  N2: part.D5, part_2.CS
  N3: part.D18, part_2.SCK
  N4: part.D19, part_2.MISO
  N5: part.D23, part_2.MOSI

custom parts:
  DOIT Esp32 DevKit v1 (30 pins long, 11 pins width): The DOIT Esp32 DevKit v1 is one of the development board created by DOIT to evaluate the ESP-WROOM-32 module. It is based on the ESP32 microcontroller that boasts Wifi, Bluetooth, Ethernet and Low Power support all in a single chip. (vanepp) made breadboard work, adjusted pin numbering and labels and reduced size of schematic and cleaned up pcb. This chip is 30pins long (2 x15) and 11 pins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
  MicroSD Card Module: A common microSD card module.
  DHT22 module: DHT22 module. Pins VCC Data GND.
