# Fritzing sketch Pengukur (saved by Fritzing 0.9.3b)

parts:
  part = 1x18650 battery shield [package=THT]
  part_2 = INA219 DC Current Monitor Module
  part_3 = DOIT Esp32 DevKit v1 (30 pins long, 11 pins width) [part_number=ESP32S-PIN30]

nets:
  N1: part.pin_7, part_2.Vin+
  GND: part.pin_8, part_2.GND, part_3.GND
  VCC: part_2.VCC, part_3.3V3
  N2: part_2.SCL, part_3.D22
  N3: part_2.SDA, part_3.D21

custom parts:
  1x18650 battery shield: 1x18650 Lithium Battery Shield V3 CC CV Type-C Micro USB Mobile Power Bank DIY Module 5V 3A 3V 1A for iPhone Samsung Xiaomi.
  INA219 DC Current Monitor Module: INA219 DC Current Monitor Module Links: INA219 product information
  DOIT Esp32 DevKit v1 (30 pins long, 11 pins width): The DOIT Esp32 DevKit v1 is one of the development board created by DOIT to evaluate the ESP-WROOM-32 module. It is based on the ESP32 microcontroller that boasts Wifi, Bluetooth, Ethernet and Low Power support all in a single chip. (vanepp) made breadboard work, adjusted pin numbering and labels and reduced size of schematic and cleaned up pcb. This chip is 30pins long (2 x15) and 11 pins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
